// Logisim project Parallel_Adder.circ as structural Verilog: 3 circuits, main circuit FAC
module FAC (
  input  in_1,
  input  in_2,
  input  in_3,
  output out_4,
  output out_5
);

  wire and_1_out, and_2_out, and_3_out, xor_2_out;

  or or_1 (out_5, and_1_out, and_2_out, and_3_out);
  and and_1 (and_1_out, in_1, in_3);
  and and_2 (and_2_out, in_1, in_2);
  and and_3 (and_3_out, in_3, in_2);
  xor xor_1 (out_4, in_1, xor_2_out);
  xor xor_2 (xor_2_out, in_2, in_3);
endmodule

module Parallel_Adder (
  input  in_1,
  input  [7:0] x_7_0,
  input  [7:0] y_7_0,
  output [7:0] out_4,
  output Overflow,
  output Cout
);

  wire _0_out_5, _1_out_5, _2_out_5, _3_out_5, _4_out_5, _5_out_5, _6_out_5;

  xor xor_1 (Overflow, _6_out_5, Cout);
  FAC _7 (.out_5(Cout), .out_4(out_4[7]), .in_2(x_7_0[7]), .in_3(y_7_0[7]), .in_1(_6_out_5));
  FAC _6 (.out_5(_6_out_5), .out_4(out_4[6]), .in_2(x_7_0[6]), .in_3(y_7_0[6]), .in_1(_5_out_5));
  FAC _5 (.out_5(_5_out_5), .out_4(out_4[5]), .in_2(x_7_0[5]), .in_3(y_7_0[5]), .in_1(_4_out_5));
  FAC _4 (.out_5(_4_out_5), .out_4(out_4[4]), .in_2(x_7_0[4]), .in_3(y_7_0[4]), .in_1(_3_out_5));
  FAC _3 (.out_5(_3_out_5), .out_4(out_4[3]), .in_2(x_7_0[3]), .in_3(y_7_0[3]), .in_1(_2_out_5));
  FAC _2 (.out_5(_2_out_5), .out_4(out_4[2]), .in_2(x_7_0[2]), .in_3(y_7_0[2]), .in_1(_1_out_5));
  FAC _1 (.out_5(_1_out_5), .out_4(out_4[1]), .in_2(x_7_0[1]), .in_3(y_7_0[1]), .in_1(_0_out_5));
  FAC _0 (.out_5(_0_out_5), .out_4(out_4[0]), .in_2(x_7_0[0]), .in_3(y_7_0[0]), .in_1(in_1));
endmodule

module Sequence_Counter (
  input  Begin,
  input  End
);

  wire and_1_out, clock_1_out, s_r_ff_1_q;
  wire [1:0] counter_1_q;

  Demultiplexer #(.select(2), .width(2), .enable("false")) demultiplexer_1 ();  // open: out0, out1, out2, out3, in, sel
  Clock clock_1 (.out(clock_1_out));
  S_R_Flip_Flop s_r_ff_1 (.S(Begin), .R(End), .Q(s_r_ff_1_q));  // open: clk, Qn, preset, reset, en
  and and_1 (and_1_out, s_r_ff_1_q, clock_1_out);
  Counter #(.width(2), .max('h3)) counter_1 (
    .count(and_1_out), .Q(counter_1_q), .clk(clock_1_out));  // open: load, D, carry, clr
endmodule
