// Logisim project counter.circ as structural Verilog
module counter (
  input  in_1,
  input  in_2,
  output [1:0] out_3
);

  wire not_1_out;

  J_K_Flip_Flop j_k_ff_1 (.J(1'b1), .clk(in_1), .K(1'b1), .Q(out_3[0]), .reset(not_1_out));  // open: Qn, preset, en
  not not_1 (not_1_out, in_2);
  J_K_Flip_Flop #(.trigger("falling")) j_k_ff_2 (
    .J(1'b1), .clk(out_3[0]), .K(1'b1), .Q(out_3[1]), .reset(not_1_out));  // open: Qn, preset, en
endmodule
