// Logisim project fsc.circ as structural Verilog
module fsc (
  input  in_1,
  input  in_2,
  input  in_3,
  output out_4,
  output out_5
);

  wire and_1_out, and_2_out, and_3_out, not_1_out, xor_1_out;

  or or_1 (out_5, and_1_out, and_2_out, and_3_out);
  and and_1 (and_1_out, in_1, in_3);
  and and_2 (and_2_out, in_1, not_1_out);
  and and_3 (and_3_out, in_3, not_1_out);
  xor xor_1 (xor_1_out, in_2, in_3);
  not not_1 (not_1_out, in_2);
  xor xor_2 (out_4, xor_1_out, in_1);
endmodule

module Scazator (
  input  in_1,
  input  [7:0] in_2,
  input  [7:0] in_3,
  output [7:0] out_4,
  output out_5
);

  wire _0_out_5, _1_out_5, _2_out_5, _3_out_5, _4_out_5, _5_out_5, _6_out_5;

  fsc _7 (.out_5(out_5), .in_1(_6_out_5), .out_4(out_4[7]), .in_2(in_2[7]), .in_3(in_3[7]));
  fsc _6 (.out_5(_6_out_5), .in_1(_5_out_5), .out_4(out_4[6]), .in_2(in_2[6]), .in_3(in_3[6]));
  fsc _5 (.out_5(_5_out_5), .in_1(_4_out_5), .out_4(out_4[5]), .in_2(in_2[5]), .in_3(in_3[5]));
  fsc _4 (.out_5(_4_out_5), .in_1(_3_out_5), .out_4(out_4[4]), .in_2(in_2[4]), .in_3(in_3[4]));
  fsc _3 (.out_5(_3_out_5), .in_1(_2_out_5), .out_4(out_4[3]), .in_2(in_2[3]), .in_3(in_3[3]));
  fsc _2 (.out_5(_2_out_5), .in_1(_1_out_5), .out_4(out_4[2]), .in_2(in_2[2]), .in_3(in_3[2]));
  fsc _1 (.out_5(_1_out_5), .in_1(_0_out_5), .out_4(out_4[1]), .in_2(in_2[1]), .in_3(in_3[1]));
  fsc _0 (.out_5(_0_out_5), .in_1(in_1), .out_4(out_4[0]), .in_2(in_2[0]), .in_3(in_3[0]));
endmodule
