// Logisim project inmultire.circ as structural Verilog: 5 circuits, main circuit model de inbus
module model_de_inbus (
  input  semnal_de_control,
  input  alt_semnal_de_control,
  input  [7:0] inbus,
  output [7:0] out_4,
  output [7:0] out_5
);

  wire clock_1_out;
  wire [7:0] controlled_buffer_1_out, controlled_buffer_2_out;

  Clock clock_1 (.out(clock_1_out));
  Register register_1 (.D(controlled_buffer_1_out), .en(semnal_de_control), .Q(out_4), .clk(clock_1_out));  // open: clr
  assign controlled_buffer_1_out = semnal_de_control ? inbus : 8'bz;  // Controlled_Buffer controlled_buffer_1
  Register register_2 (
    .D(controlled_buffer_2_out), .en(alt_semnal_de_control), .Q(out_5), .clk(clock_1_out));  // open: clr
  assign controlled_buffer_2_out = alt_semnal_de_control ? inbus : 8'bz;  // Controlled_Buffer controlled_buffer_2
endmodule

module counter (
  input  in_1,
  input  in_2,
  input  in_3,
  output [1:0] out_4
);

  wire not_1_out;

  J_K_Flip_Flop j_k_ff_1 (.J(in_2), .clk(in_1), .K(in_2), .Q(out_4[0]), .reset(not_1_out));  // open: Qn, preset, en
  not not_1 (not_1_out, in_3);
  J_K_Flip_Flop #(.trigger("falling")) j_k_ff_2 (
    .J(in_2), .clk(out_4[0]), .K(in_2), .Q(out_4[1]), .reset(not_1_out));  // open: Qn, preset, en
endmodule

module Sequence_CNT (
  input  in_1,
  input  in_2,
  input  in_3,
  input  in_4,
  output out_5,
  output out_6,
  output out_7,
  output out_8
);

  wire and_1_out, and_2_out, s_r_ff_1_q;
  wire [1:0] counter_1_out_4;

  S_R_Flip_Flop s_r_ff_1 (.S(in_1), .clk(in_3), .R(in_2), .Q(s_r_ff_1_q));  // open: Qn, preset, reset, en
  counter counter_1 (.out_4(counter_1_out_4), .in_3(and_2_out), .in_1(and_1_out), .in_2(in_3));
  and and_1 (and_1_out, s_r_ff_1_q, in_3);
  and and_2 (and_2_out, in_4, s_r_ff_1_q);
  Decoder #(.select(2), .enable("false")) decoder_1 (
    .out0(out_5), .out1(out_6), .out2(out_7), .out3(out_8), .sel(counter_1_out_4));
endmodule

module Control_Unit_inmultire (
  input  Begin,
  input  CLK,
  input  nRST,
  input  Q_0,
  input  Q__1,
  input  Count7,
  output c0,
  output c1,
  output c2,
  output c3,
  output c4,
  output c5,
  output c6,
  output c7,
  output out_15
);

  wire and_1_out, and_2_out, Cycle_0_q, Cycle_1_8_q, Cycle_9_q, not_1_out, not_3_out, not_4_out, not_5_out,
       not_6_out, not_7_out, not_8_out, not_9_out, not_10_out, not_11_out, not_12_out, sequence_cnt_1_out_5,
       sequence_cnt_1_out_6, sequence_cnt_1_out_7, xor_1_out;

  S_R_Flip_Flop Cycle_0 (.S(Begin), .clk(CLK), .R(and_1_out), .Q(Cycle_0_q));  // open: Qn, preset, reset, en
  S_R_Flip_Flop Cycle_1_8 (.S(and_1_out), .clk(CLK), .R(and_2_out), .Q(Cycle_1_8_q));  // open: Qn, preset, reset, en
  S_R_Flip_Flop Cycle_9 (.S(and_2_out), .clk(CLK), .R(out_15), .Q(Cycle_9_q));  // open: Qn, preset, reset, en
  and and_1 (and_1_out, Cycle_0_q, sequence_cnt_1_out_7);
  and and_2 (and_2_out, Cycle_1_8_q, Count7, sequence_cnt_1_out_7);
  not not_1 (not_1_out, not_4_out);
  not not_2 (out_15, not_1_out);
  not not_3 (not_3_out, not_5_out);
  not not_4 (not_4_out, not_3_out);
  not not_5 (not_5_out, not_7_out);
  not not_6 (not_6_out, not_10_out);
  not not_7 (not_7_out, not_8_out);
  not not_8 (not_8_out, not_6_out);
  Sequence_CNT sequence_cnt_1 (
    .in_1(Begin), .in_2(out_15), .in_3(CLK), .in_4(nRST), .out_5(sequence_cnt_1_out_5),
    .out_6(sequence_cnt_1_out_6), .out_7(sequence_cnt_1_out_7));  // open: out_8
  not not_9 (not_9_out, not_12_out);
  not not_10 (not_10_out, not_9_out);
  not not_11 (not_11_out, c7);
  not not_12 (not_12_out, not_11_out);
  xor xor_1 (xor_1_out, Q_0, Q__1);
  and and_3 (c0, sequence_cnt_1_out_5, Cycle_0_q);
  and and_4 (c1, sequence_cnt_1_out_6, Cycle_0_q);
  and and_5 (c2, Cycle_1_8_q, sequence_cnt_1_out_5, xor_1_out);
  and and_6 (c3, c2, Q_0, ~Q__1);  // AND_Gate
  and and_7 (c4, sequence_cnt_1_out_6, Cycle_1_8_q, ~Count7);  // AND_Gate
  and and_8 (c5, sequence_cnt_1_out_5, Cycle_9_q);
  and and_9 (c6, sequence_cnt_1_out_6, Cycle_9_q);
  and and_10 (c7, sequence_cnt_1_out_7, Cycle_9_q);

  // Notes on the sheet:
  //   nr par de invertoare pt delay
endmodule

module booth_radix_2 (
  input  [7:0] inbus,
  input  in_2,
  input  in_3,
  output out_4,
  output [7:0] outbus
);

  wire A_out, and_1_out, clock_1_out, control_unit_inmultire_1_c1, control_unit_inmultire_1_c4,
       control_unit_inmultire_1_c5, control_unit_inmultire_1_c6, control_unit_inmultire_1_c7, or_1_out,
       or_2_out, Q_q8;
  wire [1:0] control_unit_inmultire_1_c0;
  wire [2:0] counter_1_q;
  wire [7:0] A_q7, controlled_buffer_1_out, controlled_buffer_3_out, controlled_buffer_5_out, M_q7,
       multiplexer_1_out, parallel_adder_1_out_4, Q_q7, xor_1_out;
  wire [7:7] control_unit_inmultire_1_c3;

  Clock clock_1 (.out(clock_1_out));
  assign controlled_buffer_1_out = control_unit_inmultire_1_c0[0] ? {8{1'b0}} : 8'bz;  // Controlled_Buffer controlled_buffer_1
  Multiplexer #(.select(2), .width(8), .enable("false")) multiplexer_1 (
    .in1(controlled_buffer_1_out), .in2(parallel_adder_1_out_4), .out(multiplexer_1_out),
    .sel(control_unit_inmultire_1_c0));  // open: in0, in3
  or or_1 (or_1_out, control_unit_inmultire_1_c0[0], control_unit_inmultire_1_c0[1]);
  or or_2 (or_2_out, control_unit_inmultire_1_c4, control_unit_inmultire_1_c5);
  // Probe on parallel_adder_1_out_4
  Shift_Register A (
    .shift(or_2_out), .in(A_q7[7]), .clk(clock_1_out), .out(A_out), .load(or_1_out),
    .d0(multiplexer_1_out[7]), .q0(A_q7[7]), .d1(multiplexer_1_out[6]), .q1(A_q7[6]),
    .d2(multiplexer_1_out[5]), .q2(A_q7[5]), .d3(multiplexer_1_out[4]), .q3(A_q7[4]),
    .d4(multiplexer_1_out[3]), .q4(A_q7[3]), .d5(multiplexer_1_out[2]), .q5(A_q7[2]),
    .d6(multiplexer_1_out[1]), .q6(A_q7[1]), .d7(multiplexer_1_out[0]), .q7(A_q7[0]));  // open: clr
  assign outbus = control_unit_inmultire_1_c6 ? A_q7 : 8'bz;  // Controlled_Buffer controlled_buffer_2
  // Probe on A_q7
  assign controlled_buffer_3_out = control_unit_inmultire_1_c1 ? inbus : 8'bz;  // Controlled_Buffer controlled_buffer_3
  Parallel_Adder parallel_adder_1 (
    .out_4(parallel_adder_1_out_4), .x_7_0(A_q7), .y_7_0(xor_1_out), .in_1(control_unit_inmultire_1_c3[7]));  // open: Overflow, Cout
  Shift_Register #(.length(9)) Q (
    .shift(or_2_out), .in(A_out), .clk(clock_1_out), .load(control_unit_inmultire_1_c1),
    .d0(controlled_buffer_3_out[7]), .q0(Q_q7[7]), .d1(controlled_buffer_3_out[6]), .q1(Q_q7[6]),
    .d2(controlled_buffer_3_out[5]), .q2(Q_q7[5]), .d3(controlled_buffer_3_out[4]), .q3(Q_q7[4]),
    .d4(controlled_buffer_3_out[3]), .q4(Q_q7[3]), .d5(controlled_buffer_3_out[2]), .q5(Q_q7[2]),
    .d6(controlled_buffer_3_out[1]), .q6(Q_q7[1]), .d7(controlled_buffer_3_out[0]), .q7(Q_q7[0]), .d8(1'b0),
    .q8(Q_q8));  // open: out, clr
  // Probe on xor_1_out
  assign outbus = control_unit_inmultire_1_c7 ? Q_q7 : 8'bz;  // Controlled_Buffer controlled_buffer_4
  assign xor_1_out = M_q7 ^ {8{control_unit_inmultire_1_c3[7]}};  // XOR_Gate xor_1, 8 bits wide
  Counter #(.width(3), .max('h7)) counter_1 (
    .load(control_unit_inmultire_1_c0[0]), .D(3'b000), .count(control_unit_inmultire_1_c4), .Q(counter_1_q),
    .clk(clock_1_out));  // open: carry, clr
  // Probe on counter_1_q
  and and_1 (and_1_out, counter_1_q[2], counter_1_q[1], counter_1_q[0]);
  Control_Unit_inmultire control_unit_inmultire_1 (
    .Begin(in_2), .nRST(in_3), .Q_0(Q_q7[0]), .Q__1(Q_q8), .Count7(and_1_out),
    .c0(control_unit_inmultire_1_c0[0]), .c1(control_unit_inmultire_1_c1),
    .c2(control_unit_inmultire_1_c0[1]), .c3(control_unit_inmultire_1_c3[7]),
    .c4(control_unit_inmultire_1_c4), .c5(control_unit_inmultire_1_c5), .c6(control_unit_inmultire_1_c6),
    .CLK(clock_1_out), .out_15(out_4), .c7(control_unit_inmultire_1_c7));
  assign controlled_buffer_5_out = control_unit_inmultire_1_c0[0] ? inbus : 8'bz;  // Controlled_Buffer controlled_buffer_5
  Shift_Register M (
    .shift(1'b0), .clk(clock_1_out), .load(control_unit_inmultire_1_c0[0]), .d0(controlled_buffer_5_out[7]),
    .q0(M_q7[7]), .d1(controlled_buffer_5_out[6]), .q1(M_q7[6]), .d2(controlled_buffer_5_out[5]),
    .q2(M_q7[5]), .d3(controlled_buffer_5_out[4]), .q3(M_q7[4]), .d4(controlled_buffer_5_out[3]),
    .q4(M_q7[3]), .d5(controlled_buffer_5_out[2]), .q5(M_q7[2]), .d6(controlled_buffer_5_out[1]),
    .q6(M_q7[1]), .d7(controlled_buffer_5_out[0]), .q7(M_q7[0]));  // open: in, out, clr
  // Probe on control_unit_inmultire_1_c3[7]

  // Notes on the sheet:
  //   01
  //   10
  //   c4
  //   c5
  //   c0
  //   shift
  //   A[7]=A[7]
  //   c2
  //   c1
  //   c3
  //   Q[0]Q[-1]
  //   c0
  //   c4
  //   EXOR wordgate
  //   COUNT7
  //   c0
  //   c3
endmodule
