// Logisim project seqCNT.circ as structural Verilog: 3 circuits, main circuit model de inbus
module model_de_inbus (
  input  in_1,
  input  in_2,
  input  [7:0] inbus,
  output [7:0] out_4,
  output [7:0] out_5
);

  wire clock_1_out;
  wire [7:0] controlled_buffer_1_out, controlled_buffer_2_out;

  Clock clock_1 (.out(clock_1_out));
  Register register_1 (.D(controlled_buffer_1_out), .en(in_1), .Q(out_4), .clk(clock_1_out));  // open: clr
  assign controlled_buffer_1_out = in_1 ? inbus : 8'bz;  // Controlled_Buffer controlled_buffer_1
  Register register_2 (.D(controlled_buffer_2_out), .en(in_2), .Q(out_5), .clk(clock_1_out));  // open: clr
  assign controlled_buffer_2_out = in_2 ? inbus : 8'bz;  // Controlled_Buffer controlled_buffer_2
endmodule

module counter (
  input  in_1,
  input  in_2,
  input  in_3,
  output [1:0] out_4
);

  wire not_1_out;

  J_K_Flip_Flop j_k_ff_1 (.J(in_2), .clk(in_1), .K(in_2), .Q(out_4[0]), .reset(not_1_out));  // open: Qn, preset, en
  not not_1 (not_1_out, in_3);
  J_K_Flip_Flop #(.trigger("falling")) j_k_ff_2 (
    .J(in_2), .clk(out_4[0]), .K(in_2), .Q(out_4[1]), .reset(not_1_out));  // open: Qn, preset, en
endmodule

module Sequence_CNT (
  input  in_1,
  input  in_2,
  input  in_3,
  input  in_4,
  output out_5,
  output out_6,
  output out_7
);

  wire and_1_out, and_2_out, s_r_ff_1_q;
  wire [1:0] counter_1_out_4;

  S_R_Flip_Flop s_r_ff_1 (.S(in_1), .clk(in_3), .R(in_2), .Q(s_r_ff_1_q));  // open: Qn, preset, reset, en
  counter counter_1 (.out_4(counter_1_out_4), .in_3(and_2_out), .in_1(and_1_out), .in_2(in_3));
  and and_1 (and_1_out, s_r_ff_1_q, in_3);
  and and_2 (and_2_out, in_4, s_r_ff_1_q);
  Decoder #(.select(2), .enable("false")) decoder_1 (
    .out0(out_5), .out1(out_6), .out2(out_7), .sel(counter_1_out_4));  // open: out3
endmodule
